// Logisim project EX1.circ as structural Verilog: 1 circuit, main circuit main
module main (
  input  X,
  input  Y,
  output OUT1,
  output OUT2
);

  wire and_1_out;

  and and_1 (and_1_out, ~X, Y);  // AND_Gate
  or or_1 (OUT1, and_1_out, X);
  or or_2 (OUT2, X, Y);
endmodule
