// Logisim project EX2.circ as structural Verilog: 4 circuits, main circuit A
module A (
  input  X,
  input  Y,
  output OUT1,
  output OUT2
);

  wire not_1_out, not_2_out, or_1_out;

  not not_1 (not_1_out, X);
  not not_2 (not_2_out, Y);
  or or_1 (or_1_out, X, Y);
  and and_1 (OUT2, not_1_out, not_2_out);
  not not_3 (OUT1, or_1_out);
endmodule

module B (
  input  X,
  input  Y,
  output OUT1,
  output OUT2
);

  wire and_1_out, not_1_out, not_2_out;

  not not_1 (not_1_out, X);
  not not_2 (not_2_out, Y);
  and and_1 (and_1_out, X, Y);
  or or_1 (OUT2, not_1_out, not_2_out);
  not not_3 (OUT1, and_1_out);
endmodule

module C (
  input  X,
  input  Y,
  input  Z,
  output OUT1,
  output OUT2
);

  wire and_1_out, or_1_out, or_2_out;

  and and_1 (and_1_out, Y, Z);
  or or_1 (or_1_out, X, Y);
  or or_2 (or_2_out, X, Z);
  or or_3 (OUT1, X, and_1_out);
  and and_2 (OUT2, or_1_out, or_2_out);
endmodule

module D (
  input  X,
  input  Y,
  input  Z,
  output OUT1,
  output OUT2
);

  wire and_1_out, and_2_out, or_1_out;

  or or_1 (or_1_out, X, Y);
  and and_1 (and_1_out, X, Z);
  and and_2 (and_2_out, Y, Z);
  and and_3 (OUT1, Z, or_1_out);
  or or_2 (OUT2, and_1_out, and_2_out);
endmodule
