// Logisim project EX3.circ as structural Verilog: 5 circuits, main circuit SOP
module SOP (
  input  X5,
  input  X4,
  input  X3,
  input  X2,
  input  X1,
  input  X0,
  output Y
);

  wire and_1_out, and_2_out, and_3_out, and_4_out, and_5_out, and_6_out, and_7_out, and_8_out, and_9_out,
       and_10_out, and_11_out, and_12_out, and_13_out, and_14_out, and_15_out, not_1_out, not_2_out,
       not_3_out, not_4_out, not_5_out, not_6_out;

  not not_1 (not_1_out, X5);
  not not_2 (not_2_out, X4);
  not not_3 (not_3_out, X3);
  not not_4 (not_4_out, X2);
  not not_5 (not_5_out, X1);
  not not_6 (not_6_out, X0);
  and and_1 (and_1_out, not_1_out, not_2_out, not_3_out, not_4_out, X1, not_6_out);
  and and_2 (and_2_out, not_1_out, not_2_out, not_3_out, not_4_out, X1, X0);
  and and_3 (and_3_out, not_1_out, not_2_out, not_3_out, X2, not_5_out, X0);
  and and_4 (and_4_out, not_1_out, not_2_out, not_3_out, X2, X1, X0);
  and and_5 (and_5_out, not_1_out, not_2_out, X3, not_4_out, X1, X0);
  and and_6 (and_6_out, not_1_out, not_2_out, X3, X2, not_5_out, X0);
  and and_7 (and_7_out, not_1_out, X4, not_3_out, not_4_out, not_5_out, X0);
  and and_8 (and_8_out, not_1_out, X4, not_3_out, not_4_out, X1, X0);
  and and_9 (and_9_out, not_1_out, X4, not_3_out, X2, X1, X0);
  and and_10 (and_10_out, not_1_out, X4, X3, X2, not_5_out, X0);
  and and_11 (and_11_out, not_1_out, X4, X3, X2, X1, X0);
  and and_12 (and_12_out, X5, not_2_out, not_3_out, X2, not_5_out, X0);
  and and_13 (and_13_out, X5, not_2_out, X3, not_4_out, not_5_out, X0);
  and and_14 (and_14_out, X5, not_2_out, X3, not_4_out, X1, X0);
  and and_15 (and_15_out, X5, not_2_out, X3, X2, X1, X0);
  or or_1 (Y, and_1_out, and_2_out, and_3_out, and_4_out, and_5_out, and_6_out, and_7_out, and_8_out, and_9_out, and_10_out, and_11_out, and_12_out, and_13_out, and_14_out, and_15_out);
endmodule

module SOP_TEST (
  output [5:0] out_1,
  output out_2
);

  wire clock_1_out;

  Clock clock_1 (.out(clock_1_out));
  Counter #(.max('h32), .width(6)) counter_1 (.Q(out_1), .clk(clock_1_out));  // open: load, D, count, carry, up, clr
  SOP sop_1 (.X5(out_1[5]), .X4(out_1[4]), .X3(out_1[3]), .X2(out_1[2]), .X1(out_1[1]), .X0(out_1[0]), .Y(out_2));
endmodule

module POS (
  input  X5,
  input  X4,
  input  X3,
  input  X2,
  input  X1,
  input  X0,
  output Y
);

  wire not_1_out, not_2_out, not_3_out, not_4_out, not_5_out, or_1_out, or_2_out, or_3_out, or_4_out,
       or_5_out, or_6_out, or_7_out, or_8_out, or_9_out, or_10_out, or_11_out;

  not not_1 (not_1_out, X5);
  not not_2 (not_2_out, X4);
  not not_3 (not_3_out, X3);
  not not_4 (not_4_out, X2);
  not not_5 (not_5_out, X1);
  or or_1 (or_1_out, not_4_out, X0);
  or or_2 (or_2_out, not_3_out, X0);
  or or_3 (or_3_out, X5, X4, not_3_out, not_4_out, not_5_out);
  or or_4 (or_4_out, not_2_out, X0);
  or or_5 (or_5_out, not_2_out, X3, not_4_out, X1);
  or or_6 (or_6_out, not_2_out, not_3_out, X2);
  or or_7 (or_7_out, not_1_out, X3, not_5_out);
  or or_8 (or_8_out, not_1_out, not_3_out, not_4_out, X1);
  or or_9 (or_9_out, not_1_out, not_2_out);
  or or_10 (or_10_out, X5, X4, X2, X1);
  or or_11 (or_11_out, X4, X3, X2, X1);
  and and_1 (Y, or_1_out, or_2_out, or_3_out, or_4_out, or_5_out, or_6_out, or_7_out, or_8_out, or_9_out, or_10_out, or_11_out);
endmodule

module POS_TEST (
  output [5:0] out_1,
  output out_2
);

  wire clock_1_out;

  Clock clock_1 (.out(clock_1_out));
  Counter #(.max('h32), .width(6)) counter_1 (.Q(out_1), .clk(clock_1_out));  // open: load, D, count, carry, up, clr
  POS pos_1 (.X5(out_1[5]), .X4(out_1[4]), .X3(out_1[3]), .X2(out_1[2]), .X1(out_1[1]), .X0(out_1[0]), .Y(out_2));
endmodule

module BOTH (
  output [5:0] out_1,
  output out_2,
  output out_3
);

  wire clock_1_out;

  Clock clock_1 (.out(clock_1_out));
  Counter #(.max('h32), .width(6)) counter_1 (.Q(out_1), .clk(clock_1_out));  // open: load, D, count, carry, up, clr
  SOP sop_1 (.X5(out_1[5]), .X4(out_1[4]), .X3(out_1[3]), .X2(out_1[2]), .X1(out_1[1]), .X0(out_1[0]), .Y(out_2));
  POS pos_1 (.X5(out_1[5]), .X4(out_1[4]), .X3(out_1[3]), .X2(out_1[2]), .X1(out_1[1]), .X0(out_1[0]), .Y(out_3));
endmodule
