// Logisim project EX_4_A.circ as structural Verilog: 4 circuits, main circuit SOP
module main (
  input  A,
  input  B,
  input  C,
  input  D,
  output X
);

  wire and_1_out, and_2_out, or_1_out;

  and and_1 (and_1_out, A, B);
  or or_1 (or_1_out, C, D);
  and and_2 (and_2_out, and_1_out, or_1_out);
  not not_1 (X, and_2_out);
endmodule

module SOP (
  input  A,
  input  B,
  input  C,
  input  D,
  output X
);

  wire and_1_out, not_1_out, not_2_out, not_3_out, not_4_out;

  not not_1 (not_1_out, A);
  not not_2 (not_2_out, B);
  not not_3 (not_3_out, C);
  not not_4 (not_4_out, D);
  and and_1 (and_1_out, not_3_out, not_4_out);
  or or_1 (X, not_1_out, not_2_out, and_1_out);
endmodule

module POS (
  input  A,
  input  B,
  input  C,
  input  D,
  output X
);

  wire not_1_out, not_2_out, not_3_out, not_4_out, or_1_out, or_2_out;

  not not_1 (not_1_out, A);
  not not_2 (not_2_out, B);
  not not_3 (not_3_out, C);
  not not_4 (not_4_out, D);
  or or_1 (or_1_out, not_1_out, not_2_out, not_4_out);
  or or_2 (or_2_out, not_1_out, not_2_out, not_3_out);
  and and_1 (X, or_1_out, or_2_out);
endmodule

module VALIDATE (
  output [3:0] ABCD,
  output X_SOP,
  output X_POS
);

  wire clock_1_out;

  Clock clock_1 (.out(clock_1_out));
  Counter #(.max('hf), .width(4)) counter_1 (.Q(ABCD), .clk(clock_1_out));  // open: load, D, count, carry, up, clr
  SOP sop_1 (.A(ABCD[3]), .B(ABCD[2]), .C(ABCD[1]), .D(ABCD[0]), .X(X_SOP));
  POS pos_1 (.A(ABCD[3]), .B(ABCD[2]), .C(ABCD[1]), .D(ABCD[0]), .X(X_POS));
endmodule
