// Logisim project EX_4_B.circ as structural Verilog: 4 circuits, main circuit main
module main (
  input  A,
  input  B,
  input  C,
  input  D,
  input  E,
  output Y
);

  wire and_1_out, and_2_out, not_1_out, or_1_out;

  and and_1 (and_1_out, ~C, D, ~E);  // AND_Gate
  or or_1 (or_1_out, A, B, and_1_out);
  not not_1 (not_1_out, or_1_out);
  and and_2 (and_2_out, ~B, C, ~E);  // AND_Gate
  or or_2 (Y, not_1_out, and_2_out);
endmodule

module SOP (
  input  A,
  input  B,
  input  C,
  input  D,
  input  E,
  output Y
);

  wire and_1_out, and_2_out, nor_1_out, not_1_out, not_2_out, not_3_out;

  not not_1 (not_1_out, B);
  not not_2 (not_2_out, C);
  not not_3 (not_3_out, E);
  and and_1 (and_1_out, not_2_out, D, not_3_out);
  nor nor_1 (nor_1_out, A, B, and_1_out);
  and and_2 (and_2_out, not_1_out, C, not_3_out);
  or or_1 (Y, nor_1_out, and_2_out);
endmodule

module POS (
  input  A,
  input  B,
  input  C,
  input  D,
  input  E,
  output Y
);

  wire not_1_out, not_2_out, not_3_out, not_4_out, or_1_out, or_2_out, or_3_out;

  not not_1 (not_1_out, A);
  not not_2 (not_2_out, B);
  not not_3 (not_3_out, D);
  not not_4 (not_4_out, E);
  or or_1 (or_1_out, C, not_3_out, E);
  or or_2 (or_2_out, not_1_out, C);
  or or_3 (or_3_out, not_1_out, not_4_out);
  and and_1 (Y, or_1_out, not_2_out, or_2_out, or_3_out);
endmodule

module VALIDATE (
  output [4:0] ABCD,
  output X_SOP,
  output X_POS
);

  wire clock_1_out;

  Clock clock_1 (.out(clock_1_out));
  Counter #(.max('h1f), .width(5)) counter_1 (.Q(ABCD), .clk(clock_1_out));  // open: load, D, count, carry, up, clr
  SOP sop_1 (.A(ABCD[4]), .B(ABCD[3]), .C(ABCD[2]), .D(ABCD[1]), .E(ABCD[0]), .Y(X_SOP));
  POS pos_1 (.A(ABCD[4]), .B(ABCD[3]), .C(ABCD[2]), .D(ABCD[1]), .E(ABCD[0]), .Y(X_POS));
endmodule
