// Logisim project EX_4_C.circ as structural Verilog: 4 circuits, main circuit main
module main (
  input  M,
  input  N,
  input  P,
  input  Q,
  output Z
);

  wire and_1_out, not_1_out, or_1_out;

  or or_1 (or_1_out, M, N);
  and and_1 (and_1_out, ~P, Q);  // AND_Gate
  not not_1 (not_1_out, or_1_out);
  or or_2 (Z, not_1_out, and_1_out);
endmodule

module SOP (
  input  M,
  input  N,
  input  P,
  input  Q,
  output Z
);

  wire and_1_out, nor_1_out, not_1_out;

  not not_1 (not_1_out, P);
  nor nor_1 (nor_1_out, M, N);
  and and_1 (and_1_out, not_1_out, Q);
  or or_1 (Z, nor_1_out, and_1_out);
endmodule

module POS (
  input  M,
  input  N,
  input  P,
  input  Q,
  output Z
);

  wire not_1_out, not_2_out, not_3_out, or_1_out, or_2_out, or_3_out, or_4_out;

  not not_1 (not_1_out, M);
  not not_2 (not_2_out, N);
  not not_3 (not_3_out, P);
  or or_1 (or_1_out, not_2_out, Q);
  or or_2 (or_2_out, not_2_out, not_3_out);
  or or_3 (or_3_out, not_1_out, Q);
  or or_4 (or_4_out, not_1_out, not_3_out);
  and and_1 (Z, or_1_out, or_2_out, or_3_out, or_4_out);
endmodule

module VALIDATE (
  output [3:0] MNPQ,
  output X_SOP,
  output X_POS
);

  wire clock_1_out;

  Clock clock_1 (.out(clock_1_out));
  Counter #(.max('hf), .width(4)) counter_1 (.Q(MNPQ), .clk(clock_1_out));  // open: load, D, count, carry, up, clr
  SOP sop_1 (.M(MNPQ[3]), .N(MNPQ[2]), .P(MNPQ[1]), .Q(MNPQ[0]), .Z(X_SOP));
  POS pos_1 (.M(MNPQ[3]), .N(MNPQ[2]), .P(MNPQ[1]), .Q(MNPQ[0]), .Z(X_POS));
endmodule
