// Logisim project EX_4_D.circ as structural Verilog: 4 circuits, main circuit main
module main (
  input  M,
  input  N,
  input  P,
  output W
);

  wire and_1_out, or_1_out;

  and and_1 (and_1_out, M, N);
  or or_1 (or_1_out, P, ~N);  // OR_Gate
  and and_2 (W, and_1_out, or_1_out);
endmodule

module SOP (
  input  M,
  input  N,
  input  P,
  output W
);

  wire not_1_out, or_1_out;

  not not_1 (not_1_out, N);
  and and_1 (W, M, N, or_1_out);
  or or_1 (or_1_out, P, not_1_out);
endmodule

module POS (
  input  M,
  input  N,
  input  P,
  output W
);

  and and_1 (W, M, N, P);
endmodule

module VALIDATE (
  output [2:0] MNPQ,
  output X_SOP,
  output X_POS
);

  wire clock_1_out;

  Clock clock_1 (.out(clock_1_out));
  Counter #(.max('h7), .width(3)) counter_1 (.Q(MNPQ), .clk(clock_1_out));  // open: load, D, count, carry, up, clr
  SOP sop_1 (.M(MNPQ[0]), .N(MNPQ[1]), .P(MNPQ[2]), .W(X_SOP));
  POS pos_1 (.M(MNPQ[0]), .N(MNPQ[1]), .P(MNPQ[2]), .W(X_POS));
endmodule
